// Logisim project decoderBCD.circ as structural Verilog: 1 circuit, main circuit main
module main (
  input  in_1,
  input  in_2,
  input  in_3,
  input  in_4,
  input  in_5,
  input  in_6,
  input  in_7,
  input  in_8,
  input  in_9,
  input  in_10,
  input  in_11,
  input  in_12,
  input  in_13,
  input  in_14,
  input  in_15,
  input  in_16
);

  wire A, A_minus, a_t, And1, And2, And3, And4, And5, And6, And7, And8, And9, B, B_minus, b_t, C, C_minus,
       c_t, clk, D, D_minus, d_t, e, f, g, q0, q0_minus, q1, q1_minus, undriven;

  not not_1 (A_minus, A);
  not not_2 (B_minus, B);
  not not_3 (C_minus, C);
  not not_4 (D_minus, D);
  and and_1 (And1, B, D);
  and u_B_minus (And2, B_minus, D_minus);
  and and_2 (And3, C, D);
  and and_3 (And4, C_minus, D_minus);
  and and_4 (And5, C, D_minus);
  Clock clock_1 (.out(clk));
  and and_5 (And6, B_minus, C);
  and and_6 (And7, B, C_minus, D);
  and and_7 (And8, B, C_minus);
  and and_8 (And9, B, D_minus);
  or or_1 (a_t, A, And1, And2, C);
  or or_2 (b_t, B_minus, And3, And4);
  or or_3 (c_t, B, undriven, D, C_minus);
  or or_4 (d_t, A, And2, And7, And6, And5);
  _7_Segment_Display u_7_segment_display_1 (.g(g), .f(f), .a(a_t), .b(b_t), .e(e), .d(d_t), .c(c_t));  // open: dp
  or or_5 (e, And2, And5);
  or or_6 (f, A, And9, And4, And8);
  or or_7 (g, A, And6, And8, And5);
  J_K_Flip_Flop j_k_ff_1 (.J(1'b1), .clk(clk), .K(1'b1), .Q(q0), .Qn(q0_minus), .en(1'b1));  // open: preset, reset
  Multiplexer #(.select(2), .enable("false")) multiplexer_1 (
    .in0(in_16), .in1(in_12), .in2(in_8), .in3(in_4), .out(D), .sel({q1, q0}));
  J_K_Flip_Flop j_k_ff_2 (.J(q0), .clk(clk), .K(q0), .Q(q1), .Qn(q1_minus), .en(1'b1));  // open: preset, reset
  Multiplexer #(.select(2), .enable("false")) multiplexer_2 (
    .in0(in_15), .in1(in_11), .in2(in_7), .in3(in_3), .out(C), .sel({q1, q0}));
  Multiplexer #(.select(2), .enable("false")) multiplexer_3 (
    .in0(in_14), .in1(in_10), .in2(in_6), .in3(in_2), .out(B), .sel({q1, q0}));
  Multiplexer #(.select(2), .enable("false")) multiplexer_4 (
    .in0(in_13), .in1(in_9), .in2(in_5), .in3(in_1), .out(A), .sel({q1, q0}));

  // Other names for the same wires on the sheet: O0 = A; O1 = B; O2 = C; O3 = D; x0 = in_16; x1 = in_15; x2 = in_14;
  //   x3 = in_13; x4 = in_12; x5 = in_11; x6 = in_10; x7 = in_9; x8 = in_8; x9 = in_7; x10 = in_6; x11 = in_5;
  //   x12 = in_4; x13 = in_3; x14 = in_2; x15 = in_1

  // Notes on the sheet:
  //   DECODER
  //   FUNCIONAMIENTO
endmodule
